// Logisim project CU.circ as structural Verilog: 4 circuits, main circuit main
module main (
);

  wire and_1_out, clock_1_out, nand_1_out, not_1_out, or_1_out, t_ff_1_q, t_ff_1_qn, t_ff_2_q, undriven;

  not not_1 (not_1_out, t_ff_2_q);
  nand nand_1 (nand_1_out, not_1_out, t_ff_1_q);
  and and_1 (and_1_out, nand_1_out, clock_1_out);
  Clock clock_1 (.out(clock_1_out));
  T_Flip_Flop t_ff_1 (.T(1'b1), .clk(or_1_out), .Q(t_ff_1_q), .Qn(t_ff_1_qn));  // open: reset, preset
  or or_1 (or_1_out, and_1_out, undriven);
  T_Flip_Flop t_ff_2 (.T(1'b1), .clk(t_ff_1_qn), .Q(t_ff_2_q));  // open: Qn, reset, preset
endmodule

module OP_ROM (
  input  [7:0] IRin,
  output ADD,
  output SUB,
  output MULT,
  output LD,
  output SAV,
  output BEQ,
  output BNQ,
  output PRT,
  output INP,
  output STOP,
  output FLSH
);

  wire not_1_out, not_2_out, not_3_out, not_4_out, not_5_out, not_6_out, not_7_out, not_8_out, not_9_out,
       not_10_out, not_11_out, not_12_out, not_13_out, not_14_out, not_15_out, not_16_out, not_17_out,
       not_18_out, not_19_out;

  not not_1 (not_1_out, IRin[3]);
  not not_2 (not_2_out, IRin[4]);
  not not_3 (not_3_out, IRin[5]);
  not not_4 (not_4_out, IRin[4]);
  not not_5 (not_5_out, IRin[5]);
  not not_6 (not_6_out, IRin[5]);
  not not_7 (not_7_out, IRin[6]);
  not not_8 (not_8_out, IRin[6]);
  not not_9 (not_9_out, IRin[6]);
  not not_10 (not_10_out, IRin[7]);
  not not_11 (not_11_out, IRin[7]);
  not not_12 (not_12_out, IRin[2]);
  not not_13 (not_13_out, IRin[3]);
  not not_14 (not_14_out, IRin[5]);
  not not_15 (not_15_out, IRin[3]);
  not not_16 (not_16_out, IRin[5]);
  not not_17 (not_17_out, IRin[5]);
  not not_18 (not_18_out, IRin[0]);
  not not_19 (not_19_out, IRin[5]);
  and and_1 (ADD, not_1_out, not_2_out, not_3_out, IRin[6], IRin[7]);
  and and_2 (SUB, IRin[3], not_4_out, not_5_out, IRin[6], IRin[7]);
  and and_3 (MULT, IRin[5], IRin[6], IRin[7]);
  and and_4 (LD, not_6_out, not_7_out, IRin[7]);
  and and_5 (SAV, IRin[5], not_8_out, IRin[7]);
  and and_6 (BEQ, not_9_out, not_10_out);
  and and_7 (BNQ, IRin[6], not_11_out);
  and and_8 (PRT, not_12_out, not_13_out, IRin[4], not_14_out, IRin[6], IRin[7]);
  and and_9 (INP, IRin[2], not_15_out, IRin[4], not_16_out, IRin[6], IRin[7]);
  and and_10 (STOP, IRin[0], IRin[1], IRin[2], IRin[3], IRin[4], not_17_out, IRin[6], IRin[7]);
  and and_11 (FLSH, not_18_out, IRin[1], IRin[2], IRin[3], IRin[4], not_19_out, IRin[6], IRin[7]);
endmodule

module CU (
  input  [7:0] IRin,
  output Reg0,
  output Reg1,
  output ALU_L,
  output ALU_R,
  output ALU_O,
  output STAT,
  output IR,
  output PC,
  output MAR,
  output MBR,
  output R_W,
  output ALU_FLAG
);

  wire clock_1_out, t_ff_1_q, t_ff_1_qn, t_ff_2_q;

  OP_ROM op_rom_1 (.IRin(IRin));  // open: PRT, BEQ, LD, SUB, ADD, MULT, SAV, BNQ, INP, STOP, FLSH
  T_Flip_Flop t_ff_1 (.T(1'b1), .clk(clock_1_out), .Q(t_ff_1_q), .Qn(t_ff_1_qn));  // open: reset, preset
  Clock clock_1 (.out(clock_1_out));
  T_Flip_Flop t_ff_2 (.T(1'b1), .clk(t_ff_1_qn), .Q(t_ff_2_q));  // open: Qn, reset, preset

  // Notes on the sheet:
  //   Control Gates
endmodule

module ADD (
  input  [7:0] IRin,
  input  GET,
  input  EXE,
  input  SAV,
  output R0,
  output R1,
  output ALU_O,
  output R_W,
  output ALU_FLAG
);

  wire not_1_out, not_2_out, or_1_out, or_2_out;

  not not_1 (not_1_out, IRin[1]);
  not not_2 (not_2_out, IRin[2]);
  or or_1 (or_1_out, IRin[1], IRin[2]);
  or or_2 (or_2_out, not_1_out, not_2_out);
  and and_1 (R0, or_1_out, GET);
  and and_2 (R1, or_2_out, GET);
  or or_3 (ALU_O, EXE, SAV);

  assign ALU_FLAG = 1'b1;
  assign R_W = SAV;
endmodule
